# Fritzing sketch analogWeatherStation (saved by Fritzing 0.9.3b)
breadboards: 1

parts:
  Componente1 = Arduino Uno (Rev3)
  Componente2 = Barometric Pressure Sensor - BMP180 Breakout (GY-68)
  LED1 = LED - 5mm [color="Yellow (595nm)" package="5 mm [THT]"]
  LED2 = LED - 5mm [color="Blue (470nm)" package="5 mm [THT]"]
  LED3 = RGB LED (com. cathode, rgb) [package="5 mm [THT]"]
  R2 = Resistor [tolerance=±5% resistance=220 package=THT]
  R3 = Resistor [tolerance=±5% resistance=220 package=THT]
  R4 = Resistor [tolerance=±5% resistance=220 package=THT]
  R5 = Resistor [tolerance=±5% resistance=220 package=THT]

nets:
  N1: Componente1.A4/SDA, Componente2.SDA
  N2: Componente1.A5/SCL, Componente2.SCL
  N3: Componente1.D10_PWM/SS, LED2.cathode
  N4: Componente1.D11_PWM/MOSI, LED1.cathode
  GND: Componente1.GND, Componente2.GND, LED3.common_cathode, R2.Pin_1
  N5: Componente1.D3_PWM, R5.Pin_1
  N6: Componente1.D5_PWM, R4.Pin_1
  N7: Componente1.D6_PWM, R3.Pin_1
  N8: Componente1.3V3, Componente2.3.3
  N9: LED1.anode, LED2.anode, R2.Pin_0
  N10: LED3.red_anode, R3.Pin_0
  N11: LED3.green_anode, R4.Pin_0
  N12: LED3.blue_anode, R5.Pin_0

custom parts:
  Barometric Pressure Sensor - BMP180 Breakout (GY-68): This is a simple breakout board for the BMP180, a high-precision, low-power barometric pressure sensor made by Bosch Sensortec. The range of measurement is from 300hPa to 1100hPa. The sensor can be supplied with voltage ranging from 1.8V to 3.6V. Operating temperature range is -40 to +85 °C. This particular breakout board (or perhaps the configuration) is produced by Shenzhen Keep Power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
